// Logisim project Cachegrader.circ as structural Verilog: 6 circuits, main circuit main
module main (
  input  StopOnMismatchIn,
  output MemReadOut,
  output ReadyOut,
  output DidContainOut,
  output CmdIsReadOut,
  output [7:0] ByteReadOut,
  output ClkOut,
  output halt
);

  wire CorrectValueWasReturnedOnRead, CPURead, CPUWrite, MaxIterationsReached, MemWrite, not_1_out, or_1_out,
       StopTesting;
  wire [3:0] IterationOfCurrentTest;
  wire [7:0] CPUWriteValue, MemAddress, SolutionByteRead;
  wire [9:0] CPUAddress, NumberOfCorrectReads, NumberOfHits, NumberOfMisses, TestNumber;
  wire [31:0] Line2Mem, LineFromMem;

  Clock clock_1 (.out(ClkOut));
  or or_1 (or_1_out, ReadyOut, MaxIterationsReached);
  not not_1 (not_1_out, ReadyOut);
  // Probe on CPURead
  // Probe on CPUWrite
  // Probe on CPUAddress
  // Probe on CPUWriteValue
  // Probe on LineFromMem
  Counter #(.max('h9), .width(4)) counter_1 (
    .load(ReadyOut), .up(not_1_out), .clk(ClkOut), .D(4'b0001), .carry(MaxIterationsReached),
    .Q(IterationOfCurrentTest));  // open: clr, count
  // Probe on TestNumber
  // Probe on IterationOfCurrentTest
  // Probe on NumberOfCorrectReads
  // Probe on NumberOfHits
  // Probe on NumberOfMisses
  InputGeneratorCirc inputgeneratorcirc_1 (
    .StopTestingIn(StopTesting), .GoToNextTestIn(or_1_out), .ClkIn(ClkOut), .DoneOut(halt),
    .ReadOut(CPURead), .WriteOut(CPUWrite), .AddressOut(CPUAddress), .ValueOut(CPUWriteValue),
    .TestNumberOut(TestNumber));
  // Probe on ReadyOut
  // Probe on DidContainOut
  // Probe on ByteReadOut
  // Probe on MemAddress
  // Probe on MemReadOut
  // Probe on MemWrite
  // Probe on Line2Mem
  // Probe on CmdIsReadOut
  // Probe on CorrectValueWasReturnedOnRead
  // Probe on SolutionByteRead
  // implementation implementation_1: pin names not known; wires that end beside it: CPUAddress, CPURead, CPUWrite, CPUWriteValue, LineFromMem, ClkOut, ReadyOut, DidContainOut, ByteReadOut, MemAddress, MemReadOut, MemWrite, Line2Mem
  CheckerCirc checkercirc_1 (
    .StopOnIncorrect(StopOnMismatchIn), .TestNumberIn(TestNumber), .YourByteReadIn(ByteReadOut),
    .ReadyIn(ReadyOut), .ClkIn(ClkOut), .SolutionByteReadOut(SolutionByteRead),
    .CorrectValueWasReturnedOnReadOut(CorrectValueWasReturnedOnRead), .StopTestingOut(StopTesting),
    .CmdIsReadOut(CmdIsReadOut));
  StatsTracker statstracker_1 (
    .StopTestingIn(StopTesting), .DoneTestingIn(halt),
    .CorrectByteReturnedOnReadIn(CorrectValueWasReturnedOnRead), .ReadyIn(ReadyOut),
    .ContainedIn(DidContainOut), .MemReadIn(MemReadOut), .ClkIn(ClkOut),
    .NumberOfReadsCorrectOut(NumberOfCorrectReads), .NumberOfMissesOut(NumberOfMisses),
    .NumberOfHitsOut(NumberOfHits));
  RAM #(.asyncread("true"), .dataWidth(32)) ram_1 (
    .addr(MemAddress), .we(MemWrite), .oe(MemReadOut), .clk(ClkOut), .din(Line2Mem), .dout(LineFromMem));

  // Other names for the same wires on the sheet: ByteRead[7:0] = ByteReadOut; clk = ClkOut; CmdIsRead = CmdIsReadOut;
  //   DidContain = DidContainOut; MemRead = MemReadOut; Ready = ReadyOut; StopOnMismatch = StopOnMismatchIn;
  //   TestingFinsihed = halt

  // Notes on the sheet:
  //   Inputs
  //   Load The Inputs Into Here
  //   Once Max Iterations is Reached, 9, You are Forced to the Next Test
  //   Stats
  //   Outputs
  //   SetStepOnMismatch to 1 to have the testing circuit stop on the first READ that returns back the wrong value
  //   This Is Your Answer
  //   What Value Should Have Been Returned On A Read Command
  //   Values Here Only Matter When CmdIsRead == 1
  //   Place the Solution File Inside of This Circuit
  //   Load The Contents Of Memory Into Here
endmodule

module InputGeneratorCirc (
  input  StopTestingIn,
  input  GoToNextTestIn,
  input  ClkIn,
  output DoneOut,
  output ReadOut,
  output WriteOut,
  output [9:0] AddressOut,
  output [7:0] ValueOut,
  output [9:0] TestNumberOut
);

  wire and_1_out;

  and and_1 (and_1_out, GoToNextTestIn, ~StopTestingIn, ~DoneOut);  // AND_Gate
  Counter #(.max('h3ff), .width(10)) counter_1 (
    .up(1'b1), .count(and_1_out), .clk(ClkIn), .Q(TestNumberOut));  // open: clr, load, D, carry
  ROM #(.addrWidth(10), .dataWidth(21)) rom_1 (
    .addr(TestNumberOut), .data({DoneOut, ReadOut, WriteOut, AddressOut, ValueOut}));

  // Other names for the same wires on the sheet: Value[7:0] = ValueOut; Address[9:0] = AddressOut; Write = WriteOut;
  //   Read = ReadOut; Done = DoneOut; Clk = ClkIn; GoToNextTest = GoToNextTestIn; StopTesting = StopTestingIn;
  //   TestNumber[9:0] = TestNumberOut

  // Notes on the sheet:
  //   contents of rom_1 (hex, n*v repeats v):
  //   80882 83fe6 4306b 83e0e 43701 42275 8280f 80304 41bd8 84371 43f77 41d70 4250b 44733 8253d 440d8
  //   82691 440c9 83d7c 43558 446bf 83837 842c9 43e0f 4059d 41556 80166 833b0 43a89 83142 8361c 42e66
  //   43eb6 42c00 43a0e 8165c 84682 8092a 83907 41f89 817b0 40855 82056 425e8 43ff2 8039f 42bd7 82137
  //   4416b 40273 8324a 814e4 44570 41c0f 429da 82640 8069c 8099e 414d5 41004 81beb 84113 419b1 81add
  //   83f35 425ff 829cd 40250 82945 4366d 40cc2 444f8 80814 81156 8446d 42a82 42bae 82578 41135 405d0
  //   8304b 82b3a 40972 822ba 4443a 42337 82506 80bd3 80560 83552 83955 81434 43096 43da1 81aa2 80305
  //   428e6 428cc 808a2 40e80 845f0 4215d 82765 82e29 40be5 82b74 42715 417a2 41fab 8452f 81c0a 83325
  //   44624 80205 42dfc 41333 40958 81348 42736 41069 84510 44669 826dd 8067e 408e4 44680 444e8 832ad
  //   821f8 83509 82d46 81184 432cd 80b77 4005a 440e0 81ea0 43d73 42b8c 80624 41468 42699 415ed 80fc1 0
  //   100000
endmodule

module CheckerCirc (
  input  StopOnIncorrect,
  input  [9:0] TestNumberIn,
  input  [7:0] YourByteReadIn,
  input  ReadyIn,
  input  ClkIn,
  output [7:0] SolutionByteReadOut,
  output CorrectValueWasReturnedOnReadOut,
  output StopTestingOut,
  output CmdIsReadOut
);

  wire comparator_1_eq, not_1_out, or_1_out;
  wire [9:0] subtractor_1_out;

  not not_1 (not_1_out, ReadyIn);
  or or_1 (or_1_out, not_1_out, CorrectValueWasReturnedOnReadOut);
  ROM #(.addrWidth(10), .dataWidth(9)) rom_1 (.addr(subtractor_1_out), .data({CmdIsReadOut, SolutionByteReadOut}));
  Subtractor #(.width(10)) subtractor_1 (.a(TestNumberIn), .b(10'h1), .out(subtractor_1_out));  // open: bin, bout
  StopTestingCirc stoptestingcirc_1 (
    .StopOnIncorrectIn(StopOnIncorrect), .AnswerIsCorrectIn(or_1_out), .ClkIn(ClkIn),
    .StopTestingOut(StopTestingOut));
  Comparator comparator_1 (.a(SolutionByteReadOut), .b(YourByteReadIn), .eq(comparator_1_eq));  // open: gt, lt
  and and_1 (CorrectValueWasReturnedOnReadOut, ReadyIn, comparator_1_eq, CmdIsReadOut);

  // Other names for the same wires on the sheet: SolutionByteRead[7:0] = SolutionByteReadOut;
  //   CmdIsRead = CmdIsReadOut; Clk = ClkIn; CorrectValueWasReturnedOnRead = CorrectValueWasReturnedOnReadOut;
  //   Ready = ReadyIn; StopTesting = StopTestingOut; TestNumber[9:0] = TestNumberIn;
  //   YourByteRead[7:0] = YourByteReadIn

  // Notes on the sheet:
  //   contents of rom_1 (hex, n*v repeats v):
  //   1a3 1dc 6b 125 1 75 1dc 1c3 d8 1ab 77 70 b 33 10b d8 1c3 c9 174 58 bf 153 199 f 9d 56 1bb 13b 89 16c
  //   180 66 b6 0 e 107 1bf 1d8 167 89 118 55 1a2 e8 f2 1c3 d7 142 6b 73 1ab 18c 70 f da 1c3 14c 1d8 d5 4
  //   1d8 16b b1 1f4 1f2 ff 1da 50 1da 6d c2 f8 155 1c6 1f8 82 ae 1ff 35 d0 16b 1ae 72 175 3a 37 1ff 173
  //   1d0 158 167 1d5 96 a1 1f4 1c3 e6 cc 155 80 170 5d 1e6 166 e5 1ae 15 a2 ab 170 10f 13b 24 150 fc 33
  //   58 133 36 69 170 69 1c3 14c e4 80 e8 1ab 15d 158 1fc 135 cd 1e5 5a e0 104 73 8c 14c 68 99 ed 1a6
  //   After Loading the test, right click the ROM and 
  //   Select Edit Contents To Make Sure It Was Loaded Correctly
endmodule

module StopTestingCirc (
  input  StopOnIncorrectIn,
  input  AnswerIsCorrectIn,
  input  ClkIn,
  output StopTestingOut
);

  wire SavedStopTesting, StopTesting;

  and and_1 (StopTesting, ~AnswerIsCorrectIn, StopOnIncorrectIn);  // AND_Gate
  Register #(.width(1)) register_1 (.D(StopTesting), .en(StopTesting), .clk(ClkIn), .Q(SavedStopTesting));  // open: clr
  or or_1 (StopTestingOut, StopTesting, SavedStopTesting);

  // Other names for the same wires on the sheet: AnswerIsCorrect = AnswerIsCorrectIn; clk = ClkIn;
  //   StopOnIncorrect = StopOnIncorrectIn
endmodule

module StatsTracker (
  input  StopTestingIn,
  input  DoneTestingIn,
  input  CorrectByteReturnedOnReadIn,
  input  ReadyIn,
  input  ContainedIn,
  input  MemReadIn,
  input  ClkIn,
  output [9:0] NumberOfReadsCorrectOut,
  output [9:0] NumberOfMissesOut,
  output [9:0] NumberOfHitsOut
);

  wire and_2_out, and_3_out, OkToCount;

  and and_1 (OkToCount, ~StopTestingIn, ~DoneTestingIn);  // AND_Gate
  and and_2 (and_2_out, CorrectByteReturnedOnReadIn, OkToCount);
  and and_3 (and_3_out, OkToCount, ReadyIn, ContainedIn);
  Counter #(.max('h3ff), .ongoal("stay"), .width(10)) counter_1 (
    .up(1'b1), .count(and_2_out), .clk(ClkIn), .Q(NumberOfReadsCorrectOut));  // open: clr, load, D, carry
  Counter #(.max('h3ff), .ongoal("stay"), .width(10)) counter_2 (
    .up(1'b1), .count(and_3_out), .clk(ClkIn), .Q(NumberOfHitsOut));  // open: clr, load, D, carry
  Counter #(.max('h3ff), .ongoal("stay"), .width(10)) counter_3 (
    .up(1'b1), .count(MemReadIn), .clk(ClkIn), .Q(NumberOfMissesOut));  // open: clr, load, D, carry

  // Other names for the same wires on the sheet: Clk = ClkIn; Contained = ContainedIn;
  //   CorrectByteReturnedOnRead = CorrectByteReturnedOnReadIn; DoneTesting = DoneTestingIn; MemRead = MemReadIn;
  //   NumberOfHits[9:0] = NumberOfHitsOut; NumberOfMisses[9:0] = NumberOfMissesOut;
  //   NumberOfReadsCorrect[9:0] = NumberOfReadsCorrectOut; Ready = ReadyIn; StopTesting = StopTestingIn
endmodule

module newnewstate1 (
  input  S2,
  input  S1,
  input  S0,
  input  read,
  input  write,
  input  contains,
  input  dirty,
  output s2_next,
  output s1_next,
  output s0_next
);

  wire and_1_out, and_2_out, and_3_out, and_4_out, and_5_out, and_6_out, and_7_out, and_8_out, and_9_out,
       and_10_out, and_11_out, and_12_out, and_13_out, and_14_out, and_15_out, and_16_out, and_17_out,
       and_18_out, and_19_out, and_20_out, and_21_out, and_22_out, and_23_out, and_24_out, and_25_out,
       and_26_out, not_1_out, not_2_out, not_3_out, not_4_out, not_5_out, not_6_out;

  not not_1 (not_1_out, S2);
  not not_2 (not_2_out, S1);
  not not_3 (not_3_out, S0);
  not not_4 (not_4_out, read);
  not not_5 (not_5_out, write);
  not not_6 (not_6_out, dirty);
  and and_1 (and_1_out, not_1_out, S1, not_3_out, not_4_out, dirty);
  and and_2 (and_2_out, not_1_out, S1, not_3_out, not_5_out, dirty);
  and and_3 (and_3_out, not_1_out, S1, not_3_out, not_4_out, contains);
  and and_4 (and_4_out, not_1_out, S1, not_3_out, not_5_out, contains);
  and and_5 (and_5_out, S1, S0, not_4_out, write);
  and and_6 (and_6_out, S1, S0, read, not_5_out);
  and and_7 (and_7_out, S2, not_2_out, not_3_out);
  and and_8 (and_8_out, S2, not_3_out, not_4_out, not_5_out);
  and and_9 (and_9_out, S2, not_3_out, read, write);
  and and_10 (and_10_out, S2, S1, S0);
  and and_11 (and_11_out, not_1_out, S0, not_4_out);
  and and_12 (and_12_out, not_1_out, S0, not_5_out);
  and and_13 (and_13_out, S1, not_3_out);
  and and_14 (and_14_out, S1, read, write);
  and and_15 (and_15_out, not_2_out, not_3_out, not_4_out, write);
  and and_16 (and_16_out, not_3_out, not_4_out, write, contains);
  and and_17 (and_17_out, not_2_out, not_3_out, read, not_5_out);
  and and_18 (and_18_out, not_3_out, read, not_5_out, not_6_out);
  and and_19 (and_19_out, S0, read, write);
  and and_20 (and_20_out, not_1_out, S1, not_4_out, not_6_out);
  and and_21 (and_21_out, not_1_out, S1, not_5_out, contains);
  and and_22 (and_22_out, not_1_out, S1, S0);
  and and_23 (and_23_out, S2, not_2_out, not_4_out);
  and and_24 (and_24_out, S2, not_3_out, not_4_out, write);
  and and_25 (and_25_out, S2, read, not_5_out);
  and and_26 (and_26_out, S2, S0, not_5_out);
  or or_1 (s1_next, and_11_out, and_12_out, and_13_out, and_14_out);
  or or_2 (s2_next, and_1_out, and_2_out, and_3_out, and_4_out, and_5_out, and_6_out, and_7_out, and_8_out, and_9_out, and_10_out);
  or or_3 (s0_next, and_15_out, and_16_out, and_17_out, and_18_out, and_19_out, and_20_out, and_21_out, and_22_out, and_23_out, and_24_out, and_25_out, and_26_out);
endmodule
